// Logisim project MIPSxy.circ as structural Verilog: 6 circuits, main circuit main
module main (
  input  reset
);

  wire ALU_EQ, ALU_LESS, clock_1_out, ctrl_1_alu_add2_s, ctrlif_1_i2r7, ctrlif_1_ir0, ctrlif_1_ir1,
       ctrlif_1_ir2, ctrlif_1_ir3, ctrlif_1_ir4, ctrlif_1_ir5, ctrlif_1_ir26, ctrlif_1_ir28, ctrlif_1_ir29,
       ctrlif_1_ir30, ctrlif_1_ir31, DM_RE, DM_WE, PC_S, RF_R1E, RF_R2E, RF_WA_S, RF_WD_S, RF_WE;
  wire [4:0] multiplexer_1_out;
  wire [5:0] rom_1_data_2;
  wire [9:0] pc_1_pc11_2;
  wire [25:0] rom_1_data;
  wire [31:0] alu_1_s, bit_extender_1_out, multiplexer_2_out, multiplexer_3_out, ram_1_data, rf_1_r1d,
       rf_1_r2d;

  PC pc_1 (.ir25_0(rom_1_data), .pc_s(PC_S), .reset(reset), .pc11_2(pc_1_pc11_2));
  CTRLif ctrlif_1 (
    .ir5_0(rom_1_data[5:0]), .ir31_26(rom_1_data_2), .ir0(ctrlif_1_ir0), .ir1(ctrlif_1_ir1),
    .ir2(ctrlif_1_ir2), .ir3(ctrlif_1_ir3), .ir4(ctrlif_1_ir4), .ir5(ctrlif_1_ir5), .ir26(ctrlif_1_ir26),
    .i2r7(ctrlif_1_i2r7), .ir28(ctrlif_1_ir28), .ir29(ctrlif_1_ir29), .ir30(ctrlif_1_ir30),
    .ir31(ctrlif_1_ir31));
  CTRL ctrl_1 (
    .ir0(ctrlif_1_ir0), .ir1(ctrlif_1_ir1), .ir2(ctrlif_1_ir2), .ir3(ctrlif_1_ir3), .ir4(ctrlif_1_ir4),
    .ir5(ctrlif_1_ir5), .ir26(ctrlif_1_ir26), .ir27(ctrlif_1_i2r7), .ir28(ctrlif_1_ir28),
    .ir29(ctrlif_1_ir29), .ir30(ctrlif_1_ir30), .ir31(ctrlif_1_ir31), .rf_wa_s(RF_WA_S), .rf_wd_s(RF_WD_S),
    .rf_we(RF_WE), .rf_r1e(RF_R1E), .rf_r2e(RF_R2E), .alu_add2_s(ctrl_1_alu_add2_s), .dm_we(DM_WE),
    .dm_re(DM_RE), .pc_s(PC_S), .alu_sub(ALU_LESS), .alu_less(ALU_LESS), .alu_eq(ALU_EQ));
  ROM #(.addrWidth(10), .dataWidth(32)) rom_1 (.addr(pc_1_pc11_2), .data({rom_1_data_2, rom_1_data}));  // open: sel
  Multiplexer #(.width(5)) multiplexer_1 (
    .in0(rom_1_data[15:11]), .in1(rom_1_data[20:16]), .out(multiplexer_1_out), .sel(RF_WA_S));  // open: en
  // Probe on rom_1_data[15:0]
  // Probe on {rom_1_data_2, rom_1_data}
  Multiplexer #(.width(32)) multiplexer_2 (
    .in0(ram_1_data), .in1(alu_1_s), .out(multiplexer_2_out), .sel(RF_WD_S));  // open: en
  RF rf_1 (
    .r1a(rom_1_data[25:21]), .r2a(rom_1_data[20:16]), .we(RF_WE), .wa(multiplexer_1_out), .r1d(rf_1_r1d),
    .r2d(rf_1_r2d), .r1e(RF_R1E), .r2e(RF_R2E), .wd(multiplexer_2_out));
  // Probe on rom_1_data_2
  // Probe on rom_1_data[25:21]
  // Probe on rom_1_data[20:16]
  // Probe on rf_1_r1d
  // Probe on rf_1_r2d
  // Probe on rf_1_r1d[11:2]
  assign bit_extender_1_out = {{16{rom_1_data[15]}}, rom_1_data[15:0]};  // Bit_Extender bit_extender_1
  Multiplexer #(.width(32)) multiplexer_3 (
    .in0(bit_extender_1_out), .in1(rf_1_r2d), .out(multiplexer_3_out), .sel(ctrl_1_alu_add2_s));  // open: en
  ALU alu_1 (
    .less(ALU_LESS), .mul(ALU_LESS), .sub(ALU_LESS), .a(rf_1_r1d), .b(multiplexer_3_out), .s(alu_1_s),
    .eq(ALU_EQ));  // open: less_2
  // Probe on multiplexer_3_out
  RAM #(.addrWidth(10), .dataWidth(32), .bus("separate")) ram_1 (
    .addr(rf_1_r1d[11:2]), .din(rf_1_r2d), .data(ram_1_data), .str(DM_WE), .clk(clock_1_out), .ld(DM_RE));  // open: sel, clr
  Clock clock_1 (.out(clock_1_out));
  // Probe on alu_1_s
  // also tied to GND on the sheet: {ALU_LESS, PC_S}

  // Other names for the same wires on the sheet: ALU_MULT = ALU_LESS; ALU_SUB = ALU_LESS

  // Notes on the sheet:
  //   contents of rom_1 (hex, n*v repeats v):
  //   21ef0010 21ce000f 1ee4020 ade80000 8de90000 ad2e0000
endmodule

module ALU (
  input  less,
  input  mul,
  input  sub,
  input  [31:0] a,
  input  [31:0] b,
  output [31:0] s,
  output eq,
  output less_2
);

  wire buffer_1_out;
  wire [1:0] priority_encoder_1_out;
  wire [31:0] adder_1_out, bit_extender_1_out, multiplexer_1_out, multiplier_1_out, not_1_out;

  Multiplexer #(.width(32)) multiplexer_1 (.in0(b), .in1(not_1_out), .out(multiplexer_1_out), .sel(sub));  // open: en
  assign not_1_out = ~b;  // NOT_Gate not_1, 32 bits wide
  buf buffer_1 (buffer_1_out, sub);
  Adder #(.width(32)) adder_1 (.a(a), .b(multiplexer_1_out), .out(adder_1_out), .cin(sub));  // open: cout
  Multiplier #(.width(32)) multiplier_1 (.a(a), .b(b), .out(multiplier_1_out));  // open: cin, cout
  Comparator #(.width(32)) comparator_1 (.a(a), .b(b), .eq(eq), .lt(less_2));  // open: gt
  Priority_Encoder #(.select(2), .disabled(0)) priority_encoder_1 (
    .in0(1'b1), .in1(buffer_1_out), .in2(mul), .in3(less), .out(priority_encoder_1_out));  // open: gs, en_out, en_in
  assign bit_extender_1_out = {{31{1'b0}}, less_2};  // Bit_Extender bit_extender_1
  // Probe on priority_encoder_1_out
  Multiplexer #(.select(2), .width(32)) multiplexer_2 (
    .in0(adder_1_out), .in1(adder_1_out), .in2(multiplier_1_out), .in3(bit_extender_1_out), .out(s),
    .sel(priority_encoder_1_out));  // open: en
endmodule

module RF (
  input  r1e,
  input  [4:0] r1a,
  input  r2e,
  input  [4:0] r2a,
  input  [31:0] wd,
  input  we,
  input  [4:0] wa,
  output [31:0] r1d,
  output [31:0] r2d
);

  wire clock_1_out, E0, E1, E2, E3, E4, E5, E6, E7;
  wire [31:0] T0, T1, T2, T3, T4, T5, T6, T7;

  Register #(.width(32)) u_t0 (.D(wd), .en(E0), .Q(T0), .clk(clock_1_out));  // open: clr
  Register #(.width(32)) u_t1 (.D(wd), .en(E1), .Q(T1), .clk(clock_1_out));  // open: clr
  Register #(.width(32)) u_t2 (.D(wd), .en(E2), .Q(T2), .clk(clock_1_out));  // open: clr
  Register #(.width(32)) u_t3 (.D(wd), .en(E3), .Q(T3), .clk(clock_1_out));  // open: clr
  Clock clock_1 (.out(clock_1_out));
  Register #(.width(32)) u_t4 (.D(wd), .en(E4), .Q(T4), .clk(clock_1_out));  // open: clr
  Register #(.width(32)) u_t5 (.D(wd), .en(E5), .Q(T5), .clk(clock_1_out));  // open: clr
  Register #(.width(32)) u_t6 (.D(wd), .en(E6), .Q(T6), .clk(clock_1_out));  // open: clr
  Register #(.width(32)) u_t7 (.D(wd), .en(E7), .Q(T7), .clk(clock_1_out));  // open: clr
  Decoder #(.select(3), .disabled(0)) decoder_1 (
    .out0(E0), .out1(E1), .out2(E2), .out3(E3), .out4(E4), .out5(E5), .out6(E6), .out7(E7), .sel(wa[2:0]),
    .en(we));
  Multiplexer #(.select(3), .width(32)) multiplexer_1 (
    .in0(T0), .in1(T1), .in2(T2), .in3(T3), .in4(T4), .in5(T5), .in6(T6), .in7(T7), .out(r1d),
    .sel(r1a[2:0]), .en(r1e));
  Multiplexer #(.select(3), .width(32)) multiplexer_2 (
    .in0(T0), .in1(T1), .in2(T2), .in3(T3), .in4(T4), .in5(T5), .in6(T6), .in7(T7), .out(r2d),
    .sel(r2a[2:0]), .en(r2e));
endmodule

module PC (
  input  pc_s,
  input  reset,
  input  [25:0] ir25_0,
  output [9:0] pc11_2
);

  wire clock_1_out;
  wire [31:0] adder_1_out, multiplexer_1_out, pc_q;

  Adder #(.width(32)) adder_1 (.a({pc_q[31:12], pc11_2, pc_q[1:0]}), .b(32'h4), .out(adder_1_out));  // open: cin, cout
  Multiplexer #(.width(32)) multiplexer_1 (
    .in0(adder_1_out), .in1({adder_1_out[31:28], ir25_0, 2'b00}), .out(multiplexer_1_out), .sel(pc_s));  // open: en
  // Probe on {pc_q[31:12], pc11_2, pc_q[1:0]}
  Register #(.width(32)) pc (
    .D(multiplexer_1_out), .Q({pc_q[31:12], pc11_2, pc_q[1:0]}), .clk(clock_1_out), .clr(reset));  // open: en
  Clock clock_1 (.out(clock_1_out));
endmodule

module CTRL (
  input  ir0,
  input  ir1,
  input  ir2,
  input  ir3,
  input  ir4,
  input  ir5,
  input  ir26,
  input  ir27,
  input  ir28,
  input  ir29,
  input  ir30,
  input  ir31,
  output rf_wa_s,
  output rf_wd_s,
  output rf_we,
  output rf_r1e,
  output rf_r2e,
  output alu_add2_s,
  output dm_we,
  output dm_re,
  output pc_s,
  output alu_sub,
  output alu_less,
  output alu_eq
);

  wire and_1_out, and_2_out, and_3_out, and_4_out, and_5_out, and_6_out, and_7_out, and_8_out, and_9_out,
       and_10_out, and_11_out, and_12_out, and_13_out, and_14_out, and_15_out, and_16_out, and_17_out,
       and_18_out, and_19_out, and_20_out, and_21_out, and_22_out, and_23_out, nand_1_out, nand_2_out,
       nand_3_out, nand_4_out, nand_5_out, nand_6_out, nand_7_out, nand_8_out, nand_9_out, not_1_out,
       not_2_out, not_3_out, not_4_out, not_5_out, not_6_out, not_7_out, not_8_out, not_9_out, not_10_out,
       not_11_out, not_12_out, not_13_out, not_14_out, not_15_out, not_16_out, not_17_out;

  nand nand_1 (nand_1_out, ir30, ir29, ir28);
  nand nand_2 (nand_2_out, ir31, ir30, ir28, ir27, ir26);
  nand nand_3 (nand_3_out, ir31, ir30, ir28, ir27, ir26);
  nand nand_4 (nand_4_out, ir31, ir30, ir29, ir28, ir27, ir26, ir4, ir3, ir2, ir1, ir0);
  not not_1 (not_1_out, ir26);
  not not_2 (not_2_out, ir27);
  not not_3 (not_3_out, ir31);
  not not_4 (not_4_out, ir28);
  not not_5 (not_5_out, ir30);
  not not_6 (not_6_out, ir29);
  not not_7 (not_7_out, ir0);
  not not_8 (not_8_out, ir1);
  not not_9 (not_9_out, ir2);
  not not_10 (not_10_out, ir3);
  not not_11 (not_11_out, ir4);
  not not_12 (not_12_out, ir29);
  not not_13 (not_13_out, ir28);
  not not_14 (not_14_out, ir28);
  not not_15 (not_15_out, ir28);
  not not_16 (not_16_out, ir28);
  not not_17 (not_17_out, ir28);
  nand nand_5 (nand_5_out, ir30, ir28);
  nand nand_6 (nand_6_out, ir31, ir30, ir29, ir28, ir27, ir26, ir4, ir3, ir2, ir1, ir0);
  nand nand_7 (nand_7_out, ir31, ir30, ir29, ir28, ir27, ir26, ir4, ir3, ir2, ir1, ir0);
  nand nand_8 (nand_8_out, ir30, ir28);
  nand nand_9 (nand_9_out, ir30, ir29, ir28);
  and and_1 (and_1_out, ir31, ir27, ir26, nand_1_out);
  and and_2 (and_2_out, ir29, nand_2_out);
  and and_3 (and_3_out, ir29, nand_3_out);
  and and_4 (and_4_out, ir5, nand_4_out);
  and and_5 (and_5_out, not_1_out, ir29);
  and and_6 (and_6_out, not_2_out, ir29);
  and and_7 (and_7_out, ir29, not_3_out);
  and and_8 (and_8_out, not_4_out, ir29, ir30);
  and and_9 (and_9_out, ir28, ir29, not_5_out);
  and and_10 (and_10_out, ir26, ir27, not_6_out, ir31);
  and and_11 (and_11_out, not_7_out, ir5);
  and and_12 (and_12_out, not_8_out, ir5);
  and and_13 (and_13_out, not_9_out, ir5);
  and and_14 (and_14_out, not_10_out, ir5);
  and and_15 (and_15_out, not_11_out, ir5);
  and and_16 (and_16_out, ir5, not_12_out);
  and and_17 (and_17_out, ir4, not_13_out, ir29);
  and and_18 (and_18_out, ir3, not_14_out, ir29);
  and and_19 (and_19_out, ir2, not_15_out, ir29);
  and and_20 (and_20_out, ir1, not_16_out, ir29);
  and and_21 (and_21_out, ir0, not_17_out, ir29);
  and and_22 (and_22_out, ir31, ir29, ir27, ir26, nand_5_out);
  and and_23 (and_23_out, ir5, nand_6_out);
  and and_24 (alu_add2_s, ir5, nand_7_out);
  and and_25 (dm_we, ir31, ir29, ir27, ir26, nand_8_out);
  and and_26 (dm_re, ir31, ir27, ir26, nand_9_out);
  or or_1 (rf_wa_s, and_1_out, and_2_out);
  or or_2 (rf_wd_s, and_3_out, and_4_out);
  or or_3 (rf_we, and_5_out, and_6_out, and_7_out, and_8_out, and_9_out, and_10_out, and_11_out, and_12_out, and_13_out, and_14_out, and_15_out, and_16_out, and_17_out, and_18_out, and_19_out, and_20_out, and_21_out);
  or or_4 (rf_r2e, and_22_out, and_23_out);

  assign rf_r1e = 1'b1;
endmodule

module CTRLif (
  input  [5:0] ir5_0,
  input  [5:0] ir31_26,
  output ir0,
  output ir1,
  output ir2,
  output ir3,
  output ir4,
  output ir5,
  output ir26,
  output i2r7,
  output ir28,
  output ir29,
  output ir30,
  output ir31
);


  assign i2r7 = ir31_26[1];
  assign ir0 = ir5_0[0];
  assign ir1 = ir5_0[1];
  assign ir2 = ir5_0[2];
  assign ir3 = ir5_0[3];
  assign ir4 = ir5_0[4];
  assign ir5 = ir5_0[5];
  assign ir26 = ir31_26[0];
  assign ir28 = ir31_26[2];
  assign ir29 = ir31_26[3];
  assign ir30 = ir31_26[4];
  assign ir31 = ir31_26[5];
endmodule
